# Fritzing sketch Larvae_rig_skem (saved by Fritzing 0.9.1b)
circuit board: 10.2679cm x 7.83278cm
breadboards: 1

parts:
  Peltier = Peltier Element
  H-Bridge_top = H-Bridge [package=THT]
  VCC1 = Battery block 9V
  Termistor = LM35 Temperature Sensor [package="TO92 [THT]"]
  RGB_LED = RGB LED (com. cathode, rgb) [package="5 mm [THT]"]
  R2 = Resistor [tolerance=±5% resistance=220 package=THT]
  R3 = Resistor [tolerance=±5% resistance=220 package=THT]
  R4 = Resistor [tolerance=±5% resistance=220 package=THT]
  transistor = NPN-Transistor [package="TO92 [THT]"]
  LED2 = smd LED [color="Blue (430nm)" current=600mA package="0603 [SMD]"]
  R5 = Resistor [tolerance=±5% resistance=10 package=THT]
  Part1 = Arduino Uno (Rev3)
  LED3 = Super Flux LED blue [color=Blue]  # not connected

nets:
  N1: Peltier.pin1, H-Bridge_top.1Y
  N2: Peltier.pin2, H-Bridge_top.2Y
  N3: H-Bridge_top.1_2EN, H-Bridge_top.VCC1, Termistor.+Vs, Part1.5V
  N4: H-Bridge_top.1A, Part1.D2
  N5: H-Bridge_top.2A, Part1.D4
  N6: H-Bridge_top.VCC2, VCC1.+
  GND: H-Bridge_top.GND4, VCC1.-, Termistor.GND, RGB_LED.common_cathode, LED2.cathode, Part1.GND
  N7: Termistor.Vout, Part1.A5/SCL
  N8: RGB_LED.red_anode, R3.Pin_1
  N9: RGB_LED.green_anode, R2.Pin_1
  N10: RGB_LED.blue_anode, R4.Pin_1
  N11: R2.Pin_0, Part1.D5_PWM
  N12: R3.Pin_0, Part1.D3_PWM
  N13: R4.Pin_0, Part1.D6_PWM
  N14: transistor.E, R5.Pin_1
  N15: transistor.B, Part1.D7
  5V: transistor.C
  N16: LED2.anode, R5.Pin_0
