# Fritzing sketch flypi_bnc_usb1 (saved by Fritzing 0.9.1b)
circuit board: 5.99624cm x 6.64015cm
breadboards: 1

parts:
  arduino_nano = Arduino Nano (Rev3.0)
  HB-top = H-Bridge [package=THT]
  R1-220ohm = Resistor [tolerance=±5% resistance=220 package=THT]
  R2-220ohm = Resistor [tolerance=±5% resistance=220 package=THT]
  RGB = RGB LED (com. cathode, rgb) [package="5 mm [THT]"]
  R3-220ohm = Resistor [tolerance=±5% resistance=220 package=THT]
  R5-15Ohm = Resistor [tolerance=±5% resistance=15 package=THT]
  trans-LED2 = NPN-Transistor [package="TO92 [THT]"]
  trans-LED1 = NPN-Transistor [package="TO92 [THT]"]
  R4-15ohm = Resistor [tolerance=±5% resistance=15 package=THT]
  therm = LM35 Temperature Sensor [package="TO92 [THT]"]
  PS-LED1 = USB_MICROB_PLUG [package=micro-b-th]
  PS-peltier = USB_MICROB_PLUG [package=micro-b-th]
  PS-matrix = USB_MICROB_PLUG [package=micro-b-th]
  PS-LED2 = USB_MICROB_PLUG [package=micro-b-th]
  PS-ring = USB_MICROB_PLUG [package=micro-b-th]
  LED1 = BNC [package=bnc]
  LED2 = BNC [package=bnc]
  Peltier = BNC [package=bnc]
  ring = BNC [package=bnc]
  power2ring = BNC [package=bnc]
  power2mat = BNC [package=bnc]
  matrix = BNC [package=bnc]

nets:
  GND: arduino_nano.GND, HB-top.GND4, RGB.common_cathode, therm.GND, PS-LED1.GND, PS-peltier.GND, PS-matrix.GND, PS-LED2.GND, PS-ring.GND, LED1.GND, LED2.GND, ring.GND, power2ring.GND, power2mat.GND
  N1: arduino_nano.D4, R1-220ohm.Pin_1
  N2: arduino_nano.D5, R2-220ohm.Pin_1
  N3: arduino_nano.D6, R3-220ohm.Pin_1
  N4: arduino_nano.D7, ring.OUT
  N5: arduino_nano.D10, trans-LED1.B
  N6: arduino_nano.D11/MOSI, trans-LED2.B
  N7: arduino_nano.5V, HB-top.VCC1, therm.+Vs
  N8: arduino_nano.A4, matrix.GND
  N9: arduino_nano.A3, matrix.OUT
  N10: arduino_nano.A0, therm.Vout
  N11: arduino_nano.D13/SCK, HB-top.1_2EN
  N12: HB-top.1Y, Peltier.OUT
  N13: HB-top.2Y, Peltier.GND
  N14: HB-top.VCC2, PS-peltier.VCC
  N15: R1-220ohm.Pin_0, RGB.blue_anode
  N16: R2-220ohm.Pin_0, RGB.green_anode
  N17: RGB.red_anode, R3-220ohm.Pin_0
  N18: R5-15Ohm.Pin_0, LED2.OUT
  N19: R5-15Ohm.Pin_1, trans-LED2.E
  N20: trans-LED2.C, PS-LED2.VCC
  N21: trans-LED1.E, R4-15ohm.Pin_1
  N22: trans-LED1.C, PS-LED1.VCC
  N23: R4-15ohm.Pin_0, LED1.OUT
  N24: PS-matrix.VCC, power2mat.OUT
  N25: PS-ring.VCC, power2ring.OUT

notes:
  -The battery packs represent an external power supply of 5V and ~500mA.
  -The items with a big "N" are NPN transistors
  -The thing that looks like a mirror is the peltier element
  -The thing with the smiley face is an adafruit 8X8 led matrix with backpack
  -the blue LEDS are 3W.
  -The ring is a 12 LED adafruit LED
  -The resistors for the transparent LED are 220 Ohms each
  -The resistor for the blue LEDs are 15 Ohms each.s
