# Fritzing sketch flypi_breadboard1 (saved by Fritzing 0.9.1b)
circuit board: 4.61649cm x 5.39306cm
breadboards: 1

parts:
  arduino_nano = Arduino Nano (Rev3.0)
  HB-bot = H-Bridge [package=THT]
  R1-220ohm = Resistor [tolerance=±5% resistance=220 package=THT]
  R2-220ohm = Resistor [tolerance=±5% resistance=220 package=THT]
  RGB = RGB LED (com. cathode, rgb) [package="5 mm [THT]"]
  R3-220ohm = Resistor [tolerance=±5% resistance=220 package=THT]
  LED2 = smd LED [color="Blue (470nm)" package="1206 [SMD]"]
  R5-15Ohm = Resistor [tolerance=±5% resistance=15 package=THT]
  trans-LED2 = NPN-Transistor [package="TO92 [THT]"]
  LED1 = smd LED [color="Blue (470nm)" package="1206 [SMD]"]
  trans-LED1 = NPN-Transistor [package="TO92 [THT]"]
  R4-15ohm = Resistor [tolerance=±5% resistance=15 package=THT]
  Peltier = Peltier Element
  LED_matrix = 8x8 LED Matrix (red)
  therm = LM35 Temperature Sensor [package="TO92 [THT]"]
  PS-LED2 = Battery
  PS-Ring = Battery
  PS-matrix = Battery
  PS-LED1 = Battery
  PS-HB = Battery
  neopixel1 = Neopixel Ring 12

nets:
  GND: arduino_nano.GND, HB-bot.GND4, RGB.common_cathode, LED2.cathode, LED1.cathode, LED_matrix.-, therm.GND, PS-LED2.-, PS-Ring.-, PS-matrix.-, PS-LED1.-, PS-HB.-, neopixel1.GND
  N1: arduino_nano.D4, R1-220ohm.Pin_1
  N2: arduino_nano.D5, R2-220ohm.Pin_1
  N3: arduino_nano.D6, R3-220ohm.Pin_1
  N4: arduino_nano.D7, neopixel1.IN
  N5: arduino_nano.D10, trans-LED1.B
  N6: arduino_nano.D11/MOSI, trans-LED2.B
  N7: arduino_nano.5V, HB-bot.VCC1, therm.+Vs
  N8: arduino_nano.A4, LED_matrix.C
  N9: arduino_nano.A3, LED_matrix.D
  N10: arduino_nano.D13/SCK, HB-bot.1_2EN
  N11: HB-bot.1Y, Peltier.pin2
  N12: HB-bot.2Y, Peltier.pin1
  N13: HB-bot.VCC2, PS-HB.+
  N14: R1-220ohm.Pin_0, RGB.blue_anode
  N15: R2-220ohm.Pin_0, RGB.green_anode
  N16: RGB.red_anode, R3-220ohm.Pin_0
  N17: LED2.anode, R5-15Ohm.Pin_0
  N18: R5-15Ohm.Pin_1, trans-LED2.E
  N19: trans-LED2.C, PS-LED2.+
  N20: LED1.anode, R4-15ohm.Pin_0
  N21: trans-LED1.E, R4-15ohm.Pin_1
  N22: trans-LED1.C, PS-LED1.+
  N23: LED_matrix.+, PS-matrix.+
  N24: PS-Ring.+, neopixel1.VCC

notes:
  -The battery packs represent an external power supply of 5V and ~500mA.
  -The items with a big "N" are NPN transistors
  -The thing that looks like a mirror is the peltier element
  -The thing with the smiley face is an adafruit 8X8 led matrix with backpack
  -the blue LEDS are 3W.
  -The ring is a 12 LED adafruit LED
  -The resistors for the transparent LED are 220 Ohms each
  -The resistor for the blue LEDs are 15 Ohms each.s

custom parts:
  8x8 LED Matrix (red): 8x8 LED Matrix with I2C control (red)
  Neopixel Ring 12: Neopixel Ring x12
