# Fritzing sketch flypi_new_power_supply (saved by Fritzing 0.9.2b)
circuit board: 18.6995cm x 8.58133cm
breadboards: 1

parts:
  arduino_nano = Arduino Nano (Rev3.0)
  R1-220ohm = Resistor [tolerance=±5% resistance=220 package=THT]
  R2-220ohm = Resistor [tolerance=±5% resistance=220 package=THT]
  R3-220ohm = Resistor [tolerance=±5% resistance=220 package=THT]
  R5-15Ohm = Resistor [tolerance=±5% resistance=15 power=3W package=THT]
  trans-LED2 = NPN-Transistor [package="TO92 [THT]"]
  trans-LED1 = NPN-Transistor [package="TO92 [THT]"]
  R4-15ohm = Resistor [tolerance=±5% resistance=15 package=THT]
  RBGs-ss = screw terminal, 4 pins
  Therm+s- = screw terminal, 3 pins
  PS_LED2_-+ = Screw terminal - 2 pins [package=THT]
  LED2_-+ = Screw terminal - 2 pins [package=THT]
  LED1_+- = Screw terminal - 2 pins [package=THT]
  PS_LED1-+ = Screw terminal - 2 pins [package=THT]
  Ring_-+s+- = screw terminal, 5 pins
  U5 = L298 [package=multiwatt15]
  R1 = Resistor [tolerance=±5% resistance=1 power=18W package="0603 [SMD]"]
  R2 = Resistor [tolerance=±5% resistance=1k package=THT]
  C3 = Ceramic Capacitor [capacitance=100nF package="100 mil [THT, multilayer]"]
  Power_plug1 = Power plug
  C4 = Ceramic Capacitor [capacitance=100nF voltage=12V package="100 mil [THT, multilayer]"]
  Peltier_P+P- = Screw terminal - 2 pins [package=THT]
  TDA8139_-_Voltage_regulator = IC, SIP package, 9 pins [chip_label=IC]
  C5 = Ceramic Capacitor [capacitance=10µF voltage=12V package="100 mil [THT, multilayer]"]
  C6 = Ceramic Capacitor [capacitance=10µF voltage=12V package="100 mil [THT, multilayer]"]
  C7 = Ceramic Capacitor [capacitance=10µF voltage=5V package="100 mil [THT, multilayer]"]
  C8 = Ceramic Capacitor [capacitance=100nF voltage=5V package="100 mil [THT, multilayer]"]
  C9 = Ceramic Capacitor [capacitance=10µF voltage=5V package="100 mil [THT, multilayer]"]
  C10 = Ceramic Capacitor [capacitance=100nF voltage=12V package="100 mil [THT, multilayer]"]
  R3 = Resistor [tolerance=±5% resistance=2.2 package=THT]
  R4 = Resistor [tolerance=±5% resistance=2.2 package=THT]
  M+-SS-+ = screw terminal, 4 pins

nets:
  GND: arduino_nano.GND, arduino_nano.VIN, RBGs-ss.pin2, Therm+s-.pin3, PS_LED2_-+.pin1, LED2_-+.pin1, LED1_+-.pin2, PS_LED1-+.pin1, Ring_-+s+-.pin1, Ring_-+s+-.pin5, U5.GND, R1.Pin_1, C3.1, Power_plug1.GND, C4.1, TDA8139_-_Voltage_regulator.pin5, C5.0, C6.0, C7.1, C8.1, C9.1, C10.1, R3.Pin_0, M+-SS-+.pin3
  N1: arduino_nano.D2, U5.IN1
  N2: arduino_nano.D3, U5.IN2
  N3: arduino_nano.D4, R1-220ohm.Pin_1
  N4: arduino_nano.D5, R2-220ohm.Pin_1
  N5: arduino_nano.D6, R3-220ohm.Pin_1
  N6: arduino_nano.D7, Ring_-+s+-.pin3
  N7: arduino_nano.D10, trans-LED1.B
  N8: arduino_nano.D11/MOSI, trans-LED2.B
  N9: arduino_nano.5V, Therm+s-.pin1
  N10: arduino_nano.A7, R2.Pin_0, C3.0
  N11: arduino_nano.A4, M+-SS-+.pin1
  N12: arduino_nano.A3, M+-SS-+.pin2
  N13: arduino_nano.D13/SCK, U5.ENA
  N14: R1-220ohm.Pin_0, RBGs-ss.pin4
  N15: R2-220ohm.Pin_0, RBGs-ss.pin3
  N16: R3-220ohm.Pin_0, RBGs-ss.pin1
  N17: R5-15Ohm.Pin_0, LED2_-+.pin2
  N18: R5-15Ohm.Pin_1, trans-LED2.E
  N19: trans-LED2.C, PS_LED2_-+.pin2
  N20: trans-LED1.E, R4-15ohm.Pin_0
  N21: trans-LED1.C, PS_LED1-+.pin2
  N22: R4-15ohm.Pin_1, LED1_+-.pin1
  N23: Therm+s-.pin2, R2.Pin_1
  N24: Ring_-+s+-.pin2, Ring_-+s+-.pin4
  N25: U5.CSA, R1.Pin_0
  N26: U5.OUT1, Peltier_P+P-.pin2
  N27: U5.OUT2, Peltier_P+P-.pin1
  N28: U5.VS, Power_plug1.VCC, TDA8139_-_Voltage_regulator.pin1, TDA8139_-_Voltage_regulator.pin2, C5.1, C6.1, C10.0
  N29: U5.VLS, TDA8139_-_Voltage_regulator.pin8, C8.0, C9.0
  N30: C4.0, TDA8139_-_Voltage_regulator.pin3
  N31: TDA8139_-_Voltage_regulator.pin7, R3.Pin_1, R4.Pin_0
  N32: TDA8139_-_Voltage_regulator.pin9, C7.0, R4.Pin_1, M+-SS-+.pin4
