# Fritzing sketch flypi_scew_terminals_L298N (saved by Fritzing 0.9.1b)
circuit board: 6.51512cm x 4.51988cm
breadboards: 1

parts:
  arduino_nano = Arduino Nano (Rev3.0)
  R1-220ohm = Resistor [tolerance=±5% resistance=220 package=THT]
  R2-220ohm = Resistor [tolerance=±5% resistance=220 package=THT]
  R3-220ohm = Resistor [tolerance=±5% resistance=220 package=THT]
  R5-15Ohm = Resistor [tolerance=±5% resistance=15 package=THT]
  trans-LED2 = NPN-Transistor [package="TO92 [THT]"]
  trans-LED1 = NPN-Transistor [package="TO92 [THT]"]
  R4-15ohm = Resistor [tolerance=±5% resistance=15 package=THT]
  RBGs-ss = screw terminal, 4 pins
  Therm+s- = screw terminal, 3 pins
  M+-SS-+ = screw terminal, 6 pins
  PS_LED2_-+ = Screw terminal - 2 pins [package=THT]
  LED2_-+ = Screw terminal - 2 pins [package=THT]
  LED1_+- = Screw terminal - 2 pins [package=THT]
  PS_LED1-+ = Screw terminal - 2 pins [package=THT]
  Ring_-+s+- = screw terminal, 5 pins
  U5 = L298 [package=multiwatt15]
  C1 = Electrolytic Capacitor [capacitance=1µF voltage=10V package="100 mil [THT, electrolytic]"]
  C2 = Electrolytic Capacitor [capacitance=1µF voltage=10V package="100 mil [THT, electrolytic]"]
  Peltier_+-P+P- = screw terminal, 4 pins
  R1 = Resistor [tolerance=±5% resistance=1 package="0603 [SMD]"]

nets:
  GND: arduino_nano.GND, RBGs-ss.pin2, Therm+s-.pin3, M+-SS-+.pin2, M+-SS-+.pin5, PS_LED2_-+.pin1, LED2_-+.pin1, LED1_+-.pin2, PS_LED1-+.pin1, Ring_-+s+-.pin1, Ring_-+s+-.pin5, U5.GND, C1.-, Peltier_+-P+P-.pin2, R1.Pin_1
  N1: arduino_nano.D2, U5.IN1
  N2: arduino_nano.D3, U5.IN2
  N3: arduino_nano.D4, R1-220ohm.Pin_1
  N4: arduino_nano.D5, R2-220ohm.Pin_1
  N5: arduino_nano.D6, R3-220ohm.Pin_1
  N6: arduino_nano.D7, Ring_-+s+-.pin3
  N7: arduino_nano.D10, trans-LED1.B
  N8: arduino_nano.D11/MOSI, trans-LED2.B
  N9: arduino_nano.5V, Therm+s-.pin1
  N10: arduino_nano.A7, Therm+s-.pin2
  N11: arduino_nano.A4, arduino_nano.A3, M+-SS-+.pin3, M+-SS-+.pin4
  N12: arduino_nano.D13/SCK, U5.ENA
  N13: R1-220ohm.Pin_0, RBGs-ss.pin4
  N14: R2-220ohm.Pin_0, RBGs-ss.pin3
  N15: R3-220ohm.Pin_0, RBGs-ss.pin1
  N16: R5-15Ohm.Pin_0, LED2_-+.pin2
  N17: R5-15Ohm.Pin_1, trans-LED2.E
  N18: trans-LED2.C, PS_LED2_-+.pin2
  N19: trans-LED1.E, R4-15ohm.Pin_0
  N20: trans-LED1.C, PS_LED1-+.pin2
  N21: R4-15ohm.Pin_1, LED1_+-.pin1
  N22: M+-SS-+.pin1, M+-SS-+.pin6
  N23: Ring_-+s+-.pin2, Ring_-+s+-.pin4
  N24: U5.CSA, R1.Pin_0
  N25: U5.OUT1, U5.OUT2, Peltier_+-P+P-.pin3, Peltier_+-P+P-.pin4
  N26: U5.VS, C1.+
  N27: U5.VLS, C2.+

notes:
  -The battery packs represent an external power supply of 5V and ~500mA.
  -The items with a big "N" are NPN transistors
  -The thing that looks like a mirror is the peltier element
  -The thing with the smiley face is an adafruit 8X8 led matrix with backpack
  -the blue LEDS are 3W.
  -The ring is a 12 LED adafruit LED
  -The resistors for the transparent LED are 220 Ohms each
  -The resistor for the blue LEDs are 15 Ohms each.s
