# Fritzing sketch flypi_switching_VR (saved by Fritzing 0.9.2b)
breadboards: 3

parts:
  R1-220ohm = Resistor [tolerance=±5% resistance=220 package=THT]
  R2-220ohm = Resistor [tolerance=±5% resistance=220 package=THT]
  R3-220ohm = Resistor [tolerance=±5% resistance=220 package=THT]
  trans-LED2 = NPN-Transistor [package="TO92 [THT]"]
  trans-LED1 = NPN-Transistor [package="TO92 [THT]"]
  RBGs-ss = screw terminal, 4 pins
  Therm+s- = screw terminal, 3 pins
  LED2_-+ = Screw terminal - 2 pins [package=THT]
  LED1_-+ = Screw terminal - 2 pins [package=THT]
  U5 = L298 [package=multiwatt15]
  R2 = Resistor [tolerance=±5% resistance=1k package=THT]
  C3 = Ceramic Capacitor [capacitance=100nF package="100 mil [THT, multilayer]"]
  Power_plug1 = Power plug
  P+P- = Screw terminal - 2 pins [package=THT]
  C10 = Ceramic Capacitor [capacitance=100nF voltage=12V package="100 mil [THT, multilayer]"]
  MatrixSS-+ = screw terminal, 4 pins
  LM1-1 = LM2596 [package=multiwatt15]
  C12-1 = Electrolytic Capacitor [package="200 mil [THT, electrolytic]"]
  D1-1 = Schottky Diode [part_number=1N5817 package="300 mil [THT]"]
  L1-1 = Inductor [inductance=33µH package="400 mil [THT]"]
  C13-1 = Electrolytic Capacitor [capacitance=0.22mF voltage=16V package="100 mil [THT, electrolytic]"]
  to_pi = Screw terminal - 2 pins [package=THT]
  LM2-2 = LM2596 [package=multiwatt15]
  C14-2 = Electrolytic Capacitor [package="200 mil [THT, electrolytic]"]
  D2-2 = Schottky Diode [part_number=1N5817 package="300 mil [THT]"]
  L2-2 = Inductor [inductance=33µH package="400 mil [THT]"]
  C15-2 = Electrolytic Capacitor [capacitance=0.22mF voltage=16V package="100 mil [THT, electrolytic]"]
  Ring_-+s = screw terminal, 3 pins
  LM3-3 = LM2596 [package=multiwatt15]
  C16-3 = Electrolytic Capacitor [package="200 mil [THT, electrolytic]"]
  D3-3 = Schottky Diode [part_number=1N5817 package="300 mil [THT]"]
  L3-3 = Inductor [inductance=33µH package="400 mil [THT]"]
  C17-3 = Electrolytic Capacitor [capacitance=0.22mF voltage=16V package="100 mil [THT, electrolytic]"]
  arduino_nano = Arduino Nano (Rev3.0)
  R3 = 1 Ω Resistor high power [package=THT]
  servo1+-S = screw terminal, 3 pins

nets:
  N1: R1-220ohm.Pin_0, RBGs-ss.pin4
  N2: R1-220ohm.Pin_1, arduino_nano.D4
  N3: R2-220ohm.Pin_0, RBGs-ss.pin3
  N4: R2-220ohm.Pin_1, arduino_nano.D5
  N5: R3-220ohm.Pin_0, RBGs-ss.pin1
  N6: R3-220ohm.Pin_1, arduino_nano.D6
  N7: trans-LED2.E, LED2_-+.pin2
  N8: trans-LED2.B, arduino_nano.D11/MOSI
  N9: trans-LED2.C, trans-LED1.C, LM3-3.FDBK, L3-3.pin_1, C17-3.+
  N10: trans-LED1.E, LED1_-+.pin2
  N11: trans-LED1.B, arduino_nano.D10
  GND: RBGs-ss.pin2, Therm+s-.pin3, LED2_-+.pin1, LED1_-+.pin1, U5.GND, C3.1, Power_plug1.GND, C10.1, MatrixSS-+.pin3, LM1-1.GND, LM1-1.ENABLE, C12-1.-, D1-1.anode, C13-1.-, to_pi.pin1, LM2-2.GND, LM2-2.ENABLE, C14-2.-, D2-2.anode, C15-2.-, Ring_-+s.pin1, LM3-3.GND, LM3-3.ENABLE, C16-3.-, D3-3.anode, C17-3.-, arduino_nano.GND, R3.Pin_1, servo1+-S.pin2
  N12: Therm+s-.pin1, arduino_nano.5V
  N13: Therm+s-.pin2, R2.Pin_1
  N14: U5.CSA, R3.Pin_0
  N15: U5.OUT1, P+P-.pin2
  N16: U5.OUT2, P+P-.pin1
  VIN: U5.VS, Power_plug1.VCC, C10.0, LM1-1.Vin, C12-1.+, LM2-2.Vin, C14-2.+, LM3-3.Vin, C16-3.+, arduino_nano.VIN
  N17: U5.IN1, arduino_nano.D2
  N18: U5.ENA, arduino_nano.D13/SCK
  N19: U5.IN2, arduino_nano.D3
  N20: R2.Pin_0, C3.0, arduino_nano.A7
  N21: MatrixSS-+.pin1, arduino_nano.A4
  N22: MatrixSS-+.pin2, arduino_nano.A3
  N23: MatrixSS-+.pin4, LM2-2.FDBK, L2-2.pin_1, C15-2.+, Ring_-+s.pin2, servo1+-S.pin1
  N24: LM1-1.Vout, D1-1.cathode, L1-1.pin_0
  N25: LM1-1.FDBK, L1-1.pin_1, C13-1.+, to_pi.pin2
  N26: LM2-2.Vout, D2-2.cathode, L2-2.pin_0
  N27: Ring_-+s.pin3, arduino_nano.D7
  N28: LM3-3.Vout, D3-3.cathode, L3-3.pin_0
  N29: arduino_nano.D12/MISO, servo1+-S.pin3

custom parts:
  LM2596: LM2596 switching voltage regulator
  Electrolytic Capacitor: A small electrolytic capacitor
  1 Ω Resistor high power: High power resistor
