# Fritzing sketch flypi_switching_VR_0_1 (saved by Fritzing 0.9.2b)
circuit board: 7.89749cm x 7.03788cm
breadboards: 1

parts:
  pi-Vreg = LM2596 [package=multiwatt15]
  pi-inductor = Inductor [package="400 mil [THT]"]
  pi-220µf = Electrolytic Capacitor [capacitance=0.22mF voltage=16V package="100 mil [THT, electrolytic]"]
  pi-diode = Schottky Diode [part_number=1N5817 package="300 mil [THT]"]
  Power_plug1 = Power plug
  pi-+ = Screw terminal - 2 pins [package=THT]
  fan-+ = Screw terminal - 2 pins [package=THT]
  fan-270R = Resistor [tolerance=±5% resistance=270 package=THT]
  PW1-diode = Schottky Diode [part_number=1N5817 package="300 mil [THT]"]
  PW1-Vreg = LM2596 [package=multiwatt15]
  PW1-inductor = Inductor [package="400 mil [THT]"]
  PW1-220µf = Electrolytic Capacitor [capacitance=0.22mF voltage=16V package="100 mil [THT, electrolytic]"]
  PW2-diode = Schottky Diode [part_number=1N5817 package="300 mil [THT]"]
  PW2-Vreg = LM2596 [package=multiwatt15]
  PW2-inductor = Inductor [package="400 mil [THT]"]
  PW2-220µf = Electrolytic Capacitor [capacitance=0.22mF voltage=16V package="100 mil [THT, electrolytic]"]
  HP1-+ = Screw terminal - 2 pins [package=THT]
  pelt_H-bridge = L298 [package=multiwatt15]
  P+P- = Screw terminal - 2 pins [package=THT]
  Pelt100nf = Ceramic Capacitor [capacitance=100nF voltage=16V package="100 mil [THT, multilayer]"]
  pelt100nf = Electrolytic Capacitor [capacitance=100nF voltage=16V package="100 mil [THT, electrolytic]"]
  rgb220R3 = Resistor [tolerance=±5% resistance=220 package=THT]
  rgb220R2 = Resistor [tolerance=±5% resistance=220 package=THT]
  rgb220R1 = Resistor [tolerance=±5% resistance=220 package=THT]
  rgb_s-ss = screw terminal, 4 pins
  therm_+s- = screw terminal, 3 pins
  ther1KR = Resistor [tolerance=±5% resistance=1k package=THT]
  therm_100nf = Ceramic Capacitor [capacitance=100nF package="100 mil [THT, multilayer]"]
  M-+ss = screw terminal, 4 pins
  HP2-+ = Screw terminal - 2 pins [package=THT]
  R-+s = screw terminal, 3 pins
  HP1-270R = Resistor [tolerance=±5% resistance=270 package=THT]
  HP2-270R = Resistor [tolerance=±5% resistance=270 package=THT]
  servo-+s = screw terminal, 3 pins
  pi-680µf = Electrolytic Capacitor [voltage=16V capacitance=680µF package="200 mil [THT, electrolytic]"]
  PW1-680µf = Electrolytic Capacitor [voltage=16V capacitance=680µF package="200 mil [THT, electrolytic]"]
  PW2-680µf = Electrolytic Capacitor [voltage=16V capacitance=680µF package="200 mil [THT, electrolytic]"]
  Arduino_nano = Arduino Nano (Rev3.0)
  fan = NPN-Transistor [package="TO92 [THT]"]
  servo = NPN-Transistor [package="TO92 [THT]"]
  HP1 = NPN-Transistor [package="TO92 [THT]"]
  HP2 = NPN-Transistor [package="TO92 [THT]"]
  pelt-1R = 1 Ω Resistor high power [package=THT]

nets:
  VIN: pi-Vreg.Vin, Power_plug1.VCC, PW1-Vreg.Vin, PW2-Vreg.Vin, pelt_H-bridge.VS, Pelt100nf.1, pi-680µf.+, PW1-680µf.+, PW2-680µf.+, Arduino_nano.VIN, fan.C
  N1: pi-Vreg.Vout, pi-inductor.pin_1, pi-diode.cathode
  GND: pi-Vreg.GND, pi-Vreg.ENABLE, pi-220µf.-, pi-diode.anode, Power_plug1.GND, pi-+.pin1, fan-+.pin2, PW1-diode.anode, PW1-Vreg.GND, PW1-Vreg.ENABLE, PW1-220µf.-, PW2-diode.anode, PW2-220µf.-, HP1-+.pin1, pelt_H-bridge.GND, Pelt100nf.0, pelt100nf.-, rgb_s-ss.pin2, therm_+s-.pin3, therm_100nf.0, M-+ss.pin1, HP2-+.pin1, R-+s.pin1, servo-+s.pin1, pi-680µf.-, PW1-680µf.-, Arduino_nano.GND, pelt-1R.Pin_0
  N2: pi-Vreg.FDBK, pi-inductor.pin_0, pi-220µf.+, pi-+.pin2
  N3: fan-+.pin1, fan.E
  N4: fan-270R.Pin_0, pelt_H-bridge.ENA, Arduino_nano.D13/SCK
  N5: fan-270R.Pin_1, fan.B
  N6: PW1-diode.cathode, PW1-Vreg.Vout, PW1-inductor.pin_1
  N7: PW1-Vreg.FDBK, PW1-inductor.pin_0, PW1-220µf.+, pelt_H-bridge.VLS, pelt100nf.+, M-+ss.pin2, R-+s.pin2
  N8: PW2-diode.cathode, PW2-Vreg.Vout, PW2-inductor.pin_1
  N9: PW2-Vreg.GND, PW2-Vreg.ENABLE, PW2-680µf.-
  N10: PW2-Vreg.FDBK, PW2-inductor.pin_0, PW2-220µf.+, servo.C, HP1.C, HP2.C
  N11: HP1-+.pin2, HP1.E
  N12: pelt_H-bridge.CSA, pelt-1R.Pin_1
  N13: pelt_H-bridge.OUT1, P+P-.pin2
  N14: pelt_H-bridge.OUT2, P+P-.pin1
  N15: pelt_H-bridge.IN1, Arduino_nano.D2
  N16: pelt_H-bridge.IN2, Arduino_nano.D3
  N17: rgb220R3.Pin_0, rgb_s-ss.pin1
  N18: rgb220R3.Pin_1, Arduino_nano.D6
  N19: rgb220R2.Pin_0, rgb_s-ss.pin3
  N20: rgb220R2.Pin_1, Arduino_nano.D5
  N21: rgb220R1.Pin_0, rgb_s-ss.pin4
  N22: rgb220R1.Pin_1, Arduino_nano.D4
  N23: therm_+s-.pin1, Arduino_nano.5V
  N24: therm_+s-.pin2, ther1KR.Pin_0
  N25: ther1KR.Pin_1, therm_100nf.1, Arduino_nano.A7
  N26: M-+ss.pin3, Arduino_nano.A4
  N27: M-+ss.pin4, Arduino_nano.A3
  N28: HP2-+.pin2, HP2.E
  N29: R-+s.pin3, Arduino_nano.D7
  N30: HP1-270R.Pin_0, Arduino_nano.D10
  N31: HP1-270R.Pin_1, HP1.B
  N32: HP2-270R.Pin_0, Arduino_nano.D11/MOSI
  N33: HP2-270R.Pin_1, HP2.B
  N34: servo-+s.pin2, servo.E
  N35: servo-+s.pin3, Arduino_nano.D12/MISO
  N36: Arduino_nano.D8, servo.B

custom parts:
  LM2596: LM2596 switching voltage regulator
  Electrolytic Capacitor: A small electrolytic capacitor
  1 Ω Resistor high power: High power resistor
