# Fritzing sketch flypinew (saved by Fritzing 0.9.0b)
circuit board: 8.46667cm x 5.64444cm
breadboards: 1

parts:
  arduino_nano = Arduino Nano (Rev3.0)
  H-bridge = H-Bridge [package=THT]
  peltier = female pin header, 2 pins [form="♀ (female)"]
  Ext_pow_sup = female pin header, 2 pins [form="♀ (female)"]
  R1 = Resistor [tolerance=±5% resistance=220 package=THT]
  R2 = Resistor [tolerance=±5% resistance=220 package=THT]
  R3 = Resistor [tolerance=±5% resistance=220 package=THT]
  temp_sensor = female pin header, 3 pins [form="♀ (female)"]
  LED1 = female pin header, 2 pins [form="♀ (female)"]
  LED2 = female pin header, 2 pins [form="♀ (female)"]
  LED_matrix = female pin header, 4 pins [form="♀ (female)"]
  RGB = female pin header, 4 pins [form="♀ (female)"]
  LED_ring = female pin header, 1 pin [form="♀ (female)"]

nets:
  GND: arduino_nano.GND, H-bridge.GND1, Ext_pow_sup.pin2, temp_sensor.pin3, LED1.pin2, LED2.pin2, LED_matrix.pin3, RGB.pin2
  N1: arduino_nano.D2, H-bridge.1A
  N2: arduino_nano.D3, H-bridge.2A
  N3: arduino_nano.D4, R1.Pin_1
  N4: arduino_nano.D5, R2.Pin_1
  N5: arduino_nano.D6, R3.Pin_1
  N6: arduino_nano.D7, LED_ring.pin1
  N7: arduino_nano.D10, LED_matrix.pin2
  N8: arduino_nano.D11/MOSI, LED_matrix.pin1
  N9: arduino_nano.5V, H-bridge.1_2EN, H-bridge.VCC1, temp_sensor.pin1
  N10: arduino_nano.A0, temp_sensor.pin2
  N11: H-bridge.1Y, peltier.pin2
  N12: H-bridge.2Y, peltier.pin1
  N13: H-bridge.VCC2, Ext_pow_sup.pin1
  N14: R1.Pin_0, RGB.pin4
  N15: R2.Pin_0, RGB.pin3
  N16: R3.Pin_0, RGB.pin1
