# Fritzing sketch flypinew1 (saved by Fritzing 0.9.1b)
circuit board: 4.55359cm x 5.38682cm
breadboards: 1

parts:
  arduino_nano = Arduino Nano (Rev3.0)
  H-bridge = H-Bridge [package=THT]
  peltier = female pin header, 2 pins [form="♀ (female)"]
  PS3+- = female pin header, 2 pins [form="♀ (female)"]
  R1 = Resistor [tolerance=±5% resistance=220 package=THT]
  R2 = Resistor [tolerance=±5% resistance=220 package=THT]
  R3 = Resistor [tolerance=±5% resistance=220 package=THT]
  temp_sensor = female pin header, 3 pins [form="♀ (female)"]
  LED1+- = female pin header, 2 pins [form="♀ (female)"]
  LED2+- = female pin header, 2 pins [form="♀ (female)"]
  LEDmatrix_ss-+ = female pin header, 4 pins [form="♀ (female)"]
  RGB_s-ss = female pin header, 4 pins [form="♀ (female)"]
  Trans1 = NPN-Transistor [package="TO92 [THT]"]
  Trans2 = NPN-Transistor [package="TO92 [THT]"]
  PS2+- = female pin header, 2 pins [form="♀ (female)"]
  LEDring+-s = female pin header, 3 pins [form="♀ (female)"]
  PS5+- = female pin header, 2 pins [form="♀ (female)"]
  PS1+- = female pin header, 2 pins [form="♀ (female)"]
  R4 = Resistor [tolerance=±5% resistance=15 package=THT]
  R5 = Resistor [tolerance=±5% resistance=15 package=THT]
  PS4+- = female pin header, 2 pins [form="♀ (female)"]

nets:
  GND: arduino_nano.GND, H-bridge.GND1, H-bridge.GND4, PS3+-.pin2, temp_sensor.pin3, LED1+-.pin2, LED2+-.pin2, LEDmatrix_ss-+.pin3, RGB_s-ss.pin2, PS2+-.pin2, LEDring+-s.pin2, PS5+-.pin1, PS1+-.pin2, PS4+-.pin2
  N1: arduino_nano.D2, H-bridge.1A
  N2: arduino_nano.D3, H-bridge.2A
  N3: arduino_nano.D4, R1.Pin_1
  N4: arduino_nano.D5, R2.Pin_1
  N5: arduino_nano.D6, R3.Pin_1
  N6: arduino_nano.D7, LEDring+-s.pin1
  N7: arduino_nano.D10, Trans1.B
  N8: arduino_nano.D11/MOSI, Trans2.B
  N9: arduino_nano.5V, H-bridge.1_2EN, H-bridge.VCC1, temp_sensor.pin1
  N10: arduino_nano.A7, temp_sensor.pin2
  N11: arduino_nano.A5, LEDmatrix_ss-+.pin2
  N12: arduino_nano.A4, LEDmatrix_ss-+.pin1
  N13: H-bridge.1Y, peltier.pin2
  N14: H-bridge.2Y, peltier.pin1
  N15: H-bridge.VCC2, PS3+-.pin1
  N16: R1.Pin_0, RGB_s-ss.pin4
  N17: R2.Pin_0, RGB_s-ss.pin3
  N18: R3.Pin_0, RGB_s-ss.pin1
  N19: LED1+-.pin1, R4.Pin_0
  N20: LED2+-.pin1, R5.Pin_0
  N21: LEDmatrix_ss-+.pin4, PS4+-.pin1
  N22: Trans1.E, R4.Pin_1
  N23: Trans1.C, PS1+-.pin1
  N24: Trans2.E, R5.Pin_1
  N25: Trans2.C, PS2+-.pin1
  N26: LEDring+-s.pin3, PS5+-.pin2
