# Fritzing sketch flypi_audio_usb1 (saved by Fritzing 0.9.1b)
circuit board: 5.99624cm x 6.64015cm
breadboards: 1

parts:
  arduino_nano = Arduino Nano (Rev3.0)
  HB-top = H-Bridge [package=THT]
  R1-220ohm = Resistor [tolerance=±5% resistance=220 package=THT]
  R2-220ohm = Resistor [tolerance=±5% resistance=220 package=THT]
  RGB = RGB LED (com. cathode, rgb) [package="5 mm [THT]"]
  R3-220ohm = Resistor [tolerance=±5% resistance=220 package=THT]
  R5-15Ohm = Resistor [tolerance=±5% resistance=15 package=THT]
  trans-LED2 = NPN-Transistor [package="TO92 [THT]"]
  trans-LED1 = NPN-Transistor [package="TO92 [THT]"]
  R4-15ohm = Resistor [tolerance=±5% resistance=15 package=THT]
  therm = LM35 Temperature Sensor [package="TO92 [THT]"]
  PS-LED1 = USB_MICROB_PLUG [package=micro-b-th]
  PS-matrix = USB_MICROB_PLUG [package=micro-b-th]
  PS-LED2 = USB_MICROB_PLUG [package=micro-b-th]
  PS-ring = USB_MICROB_PLUG [package=micro-b-th]
  LED1 = BNC [package=bnc]
  LED2 = BNC [package=bnc]
  matrix = Audio Jack (TRRS) 3.5mm [part_number="LUMBERG JEITA RC-5325A" package="RC-5325A [SMD]"]
  TRRS2 = Audio Jack (TRRS) 3.5mm [part_number="LUMBERG JEITA RC-5325A" package="RC-5325A [SMD]"]
  PS-peltier = USB_MICROB_PLUG [package=micro-b-th]
  TRRS3 = Audio Jack (TRRS) 3.5mm [part_number="LUMBERG JEITA RC-5325A" package="RC-5325A [SMD]"]

nets:
  GND: arduino_nano.GND, HB-top.GND4, RGB.common_cathode, therm.GND, PS-LED1.GND, PS-matrix.GND, PS-LED2.GND, PS-ring.GND, LED1.GND, LED2.GND, matrix.SLEEVE, PS-peltier.GND, TRRS3.SLEEVE
  N1: arduino_nano.D2, HB-top.2A
  N2: arduino_nano.D4, R1-220ohm.Pin_1
  N3: arduino_nano.D5, R2-220ohm.Pin_1
  N4: arduino_nano.D6, R3-220ohm.Pin_1
  N5: arduino_nano.D7, TRRS3.RING1, TRRS3.RING2
  N6: arduino_nano.D10, trans-LED1.B
  N7: arduino_nano.D11/MOSI, trans-LED2.B
  N8: arduino_nano.5V, HB-top.VCC1, therm.+Vs
  N9: arduino_nano.A4, matrix.RING2
  N10: arduino_nano.A3, matrix.RING1
  N11: arduino_nano.A0, therm.Vout
  N12: arduino_nano.D13/SCK, HB-top.1_2EN
  N13: HB-top.1Y, TRRS2.TIP, TRRS2.RING1
  N14: HB-top.2Y, TRRS2.SLEEVE, TRRS2.RING2
  N15: HB-top.VCC2, PS-peltier.VCC
  N16: R1-220ohm.Pin_0, RGB.blue_anode
  N17: R2-220ohm.Pin_0, RGB.green_anode
  N18: RGB.red_anode, R3-220ohm.Pin_0
  N19: R5-15Ohm.Pin_0, LED2.OUT
  N20: R5-15Ohm.Pin_1, trans-LED2.E
  N21: trans-LED2.C, PS-LED2.VCC
  N22: trans-LED1.E, R4-15ohm.Pin_1
  N23: trans-LED1.C, PS-LED1.VCC
  N24: R4-15ohm.Pin_0, LED1.OUT
  N25: PS-matrix.VCC, matrix.TIP
  N26: PS-ring.VCC, TRRS3.TIP

notes:
  -The battery packs represent an external power supply of 5V and ~500mA.
  -The items with a big "N" are NPN transistors
  -The thing that looks like a mirror is the peltier element
  -The thing with the smiley face is an adafruit 8X8 led matrix with backpack
  -the blue LEDS are 3W.
  -The ring is a 12 LED adafruit LED
  -The resistors for the transparent LED are 220 Ohms each
  -The resistor for the blue LEDs are 15 Ohms each.s
