# Fritzing sketch flypi_banana1 (saved by Fritzing 0.9.1b)
breadboards: 1

parts:
  arduino_nano = Arduino Nano (Rev3.0)
  HB-top = H-Bridge [package=THT]
  R1-220ohm = Resistor [tolerance=±5% resistance=220 package=THT]
  R2-220ohm = Resistor [tolerance=±5% resistance=220 package=THT]
  R3-220ohm = Resistor [tolerance=±5% resistance=220 package=THT]
  R5-15Ohm = Resistor [tolerance=±5% resistance=15 package=THT]
  trans-LED2 = NPN-Transistor [package="TO92 [THT]"]
  trans-LED1 = NPN-Transistor [package="TO92 [THT]"]
  R4-15ohm = Resistor [tolerance=±5% resistance=15 package=THT]
  matrix = Audio Jack (TRRS) 3.5mm [part_number="LUMBERG JEITA RC-5325A" package="RC-5325A [SMD]"]
  Ring = Audio Jack (TRRS) 3.5mm [part_number="LUMBERG JEITA RC-5325A" package="RC-5325A [SMD]"]
  PS-R-vcc = BANANA_CONN [package=banana_conn]
  PS-R-gnd = BANANA_CONN [package=banana_conn]
  PS-L2-vcc = BANANA_CONN [package=banana_conn]
  PS-L2-gnd = BANANA_CONN [package=banana_conn]
  PS-M-gnd = BANANA_CONN [package=banana_conn]
  PS-M-vcc = BANANA_CONN [package=banana_conn]
  PS-P-vcc = BANANA_CONN [package=banana_conn]
  PS-P-gnd = BANANA_CONN [package=banana_conn]
  PS-L1-vcc = BANANA_CONN [package=banana_conn]
  PS-L1-gnd = BANANA_CONN [package=banana_conn]
  RGB = Audio Jack (TRRS) 3.5mm [part_number="LUMBERG JEITA RC-5325A" package="RC-5325A [SMD]"]
  Therm = Audio Jack (TRRS) 3.5mm [part_number="LUMBERG JEITA RC-5325A" package="RC-5325A [SMD]"]
  Peltier1 = BANANA_CONN [package=banana_conn]
  Peltier2 = BANANA_CONN [package=banana_conn]
  LED1_- = BANANA_CONN [package=banana_conn]
  LED1_+ = BANANA_CONN [package=banana_conn]
  LED2_- = BANANA_CONN [package=banana_conn]
  LED2_+ = BANANA_CONN [package=banana_conn]

nets:
  N1: arduino_nano.D2, HB-top.2A
  N2: arduino_nano.D4, R1-220ohm.Pin_1
  N3: arduino_nano.D5, R2-220ohm.Pin_1
  N4: arduino_nano.D6, R3-220ohm.Pin_1
  N5: arduino_nano.D7, Ring.RING1, Ring.RING2
  N6: arduino_nano.D10, trans-LED1.B
  N7: arduino_nano.D11/MOSI, trans-LED2.B
  N8: arduino_nano.5V, HB-top.VCC1
  N9: arduino_nano.A4, matrix.RING2
  N10: arduino_nano.A3, matrix.RING1
  N11: arduino_nano.A0, Therm.RING1, Therm.RING2
  N12: arduino_nano.D13/SCK, HB-top.1_2EN
  N13: HB-top.1Y, Peltier1.1
  N14: HB-top.2Y, Peltier2.1
  N15: HB-top.VCC2, PS-P-vcc.1
  N16: HB-top.GND4, matrix.SLEEVE, Ring.SLEEVE, PS-R-gnd.1, PS-L2-gnd.1, PS-M-gnd.1, PS-P-gnd.1, PS-L1-gnd.1, RGB.SLEEVE, Therm.SLEEVE, LED1_-.1, LED2_-.1
  N17: R1-220ohm.Pin_0, RGB.TIP
  N18: R2-220ohm.Pin_0, RGB.RING1
  N19: R3-220ohm.Pin_0, RGB.RING2
  N20: R5-15Ohm.Pin_0, LED2_+.1
  N21: R5-15Ohm.Pin_1, trans-LED2.E
  N22: trans-LED2.C, PS-L2-vcc.1
  N23: trans-LED1.E, R4-15ohm.Pin_1
  N24: trans-LED1.C, PS-L1-vcc.1
  N25: R4-15ohm.Pin_0, LED1_+.1
  N26: matrix.TIP, PS-M-vcc.1
  N27: Ring.TIP, PS-R-vcc.1

notes:
  -The battery packs represent an external power supply of 5V and ~500mA.
  -The items with a big "N" are NPN transistors
  -The thing that looks like a mirror is the peltier element
  -The thing with the smiley face is an adafruit 8X8 led matrix with backpack
  -the blue LEDS are 3W.
  -The ring is a 12 LED adafruit LED
  -The resistors for the transparent LED are 220 Ohms each
  -The resistor for the blue LEDs are 15 Ohms each.s
