# Fritzing sketch flypi_bnc_usb1 (saved by Fritzing 0.9.0b)
circuit board: 7.39383cm x 6.65471cm
breadboards: 1

parts:
  arduino_nano = Arduino Nano (Rev3.0)
  R1-220ohm = Resistor [tolerance=±5% resistance=220 package=THT]
  R2-220ohm = Resistor [tolerance=±5% resistance=220 package=THT]
  RGB = RGB LED (com. cathode, rgb) [package="5 mm [THT]"]
  R3-220ohm = Resistor [tolerance=±5% resistance=220 package=THT]
  R5-15Ohm = Resistor [tolerance=±5% resistance=15 package=THT]
  trans-LED2 = NPN-Transistor [package="TO92 [THT]"]
  trans-LED1 = NPN-Transistor [package="TO92 [THT]"]
  R4-15ohm = Resistor [tolerance=±5% resistance=15 package=THT]
  therm = LM35 Temperature Sensor [package="TO92 [THT]"]
  PS-LED1 = USB_MICROB_PLUG [package=micro-b-th]
  PS-peltier = USB_MICROB_PLUG [package=micro-b-th]
  PS-matrix = USB_MICROB_PLUG [package=micro-b-th]
  PS-LED2 = USB_MICROB_PLUG [package=micro-b-th]
  PS-ring = USB_MICROB_PLUG [package=micro-b-th]
  LED1 = BNC [package=bnc]
  LED2 = BNC [package=bnc]
  ring = BNC [package=bnc]
  power2ring = BNC [package=bnc]
  power2mat = BNC [package=bnc]
  matrix = BNC [package=bnc]
  Rel1 = RELAY-2 [package=relay-g5v]
  Rel2 = RELAY-2 [package=relay-g5v]
  peltier_ps = Battery block 9V
  peltier_+ = BANANA_CONN [package=banana_conn]
  peltier_- = BANANA_CONN [package=banana_conn]
  Rel3 = RELAY-2 [package=relay-g5v]
  Rel4 = RELAY-2 [package=relay-g5v]

nets:
  GND: arduino_nano.GND, RGB.common_cathode, therm.GND, PS-LED1.GND, PS-peltier.GND, PS-matrix.GND, PS-LED2.GND, PS-ring.GND, LED1.GND, LED2.GND, ring.GND, power2ring.GND, power2mat.GND, Rel1.2, Rel2.2, Rel3.2, Rel4.2
  N1: arduino_nano.D2, Rel3.9
  N2: arduino_nano.D3, Rel1.9
  N3: arduino_nano.D4, R1-220ohm.Pin_1
  N4: arduino_nano.D5, R2-220ohm.Pin_1
  N5: arduino_nano.D6, R3-220ohm.Pin_1
  N6: arduino_nano.D7, ring.OUT
  N7: arduino_nano.D10, trans-LED1.B
  N8: arduino_nano.D11/MOSI, trans-LED2.B
  N9: arduino_nano.D12/MISO, Rel4.9
  N10: arduino_nano.5V, therm.+Vs
  N11: arduino_nano.A4, matrix.GND
  N12: arduino_nano.A3, matrix.OUT
  N13: arduino_nano.A0, therm.Vout
  N14: arduino_nano.D13/SCK, Rel2.9
  N15: R1-220ohm.Pin_0, RGB.blue_anode
  N16: R2-220ohm.Pin_0, RGB.green_anode
  N17: RGB.red_anode, R3-220ohm.Pin_0
  N18: R5-15Ohm.Pin_0, LED2.OUT
  N19: R5-15Ohm.Pin_1, trans-LED2.E
  N20: trans-LED2.C, PS-LED2.VCC
  N21: trans-LED1.E, R4-15ohm.Pin_1
  N22: trans-LED1.C, PS-LED1.VCC
  N23: R4-15ohm.Pin_0, LED1.OUT
  N24: PS-matrix.VCC, power2mat.OUT
  N25: PS-ring.VCC, power2ring.OUT
  N26: Rel1.5, peltier_+.1, Rel3.6
  N27: Rel1.10, peltier_ps.+, Rel3.10
  N28: Rel2.5, peltier_-.1, Rel4.6
  N29: Rel2.10, peltier_ps.-, Rel4.10

notes:
  -The battery packs represent an external power supply of 5V and ~500mA.
  -The items with a big "N" are NPN transistors
  -The thing that looks like a mirror is the peltier element
  -The thing with the smiley face is an adafruit 8X8 led matrix with backpack
  -the blue LEDS are 3W.
  -The ring is a 12 LED adafruit LED
  -The resistors for the transparent LED are 220 Ohms each
  -The resistor for the blue LEDs are 15 Ohms each.s
